// Logisim project Priority_Encoder.circ as structural Verilog: 1 circuit, main circuit main
module main (
  input  D3,
  input  D2,
  input  D1,
  input  D0,
  output A0,
  output A1,
  output Valid
);

  wire AND1_out, not_1_out;

  not not_1 (not_1_out, D2);
  and AND1 (AND1_out, not_1_out, D1);
  or OR1 (A0, D3, AND1_out);
  or OR2 (A1, D3, D2);
  or OR3 (Valid, D3, D2, D1, D0);
endmodule
